// Logisim project Ctl_Shift_Add_Sub_Mov.circ as structural Verilog: 1 circuit, main circuit Shift_Add_Sub_Mov
module Shift_Add_Sub_Mov (
  input  [15:0] Instruction,
  input  Enable,
  output [2:0] Rm,
  output [2:0] Rn,
  output [2:0] Rd,
  output [4:0] Imm5,
  output [31:0] Imm32,
  output Imm32_Enable,
  output Carry,
  output [3:0] ALU_Opcode,
  output [3:0] Flags_Update_Mask
);

  wire ADD_I, ADD_IMM, ADD_R, ADD_SUB, and_2_out, and_3_out, and_9_out, ASR, CMP, LSL, LSR, MOVE, or_1_out,
       or_2_out, or_3_out, or_4_out, or_5_out, or_8_out, SUB_I, SUB_IMM, SUB_R;
  wire [2:0] imm3, RD1, RD2, RD3, RD4, RDN5, RM1, RM2, RN1, RN2;
  wire [7:0] imm8;
  wire [15:0] and_4_out, and_5_out, bit_extender_1_out, bit_extender_2_out, bit_extender_3_out,
       bit_extender_4_out, bit_extender_5_out, bit_extender_6_out, Instr;
  wire [15:9] and_7_out, and_8_out;
  wire [15:11] and_6_out;
  wire [31:0] bit_extender_7_out, bit_extender_8_out;

  assign bit_extender_1_out = {{15{Enable}}, Enable};  // Bit_Extender bit_extender_1
  Decoder #(.select(3)) decoder_1 (
    .out0(LSL), .out1(LSR), .out2(ASR), .out3(ADD_SUB), .out4(MOVE), .out5(CMP), .out6(ADD_IMM),
    .out7(SUB_IMM), .sel({Carry, ALU_Opcode[3:2]}));  // open: en
  Decoder #(.select(2)) decoder_2 (
    .out0(ADD_R), .out1(SUB_R), .out2(ADD_I), .out3(SUB_I), .sel(ALU_Opcode[1:0]));  // open: en
  or or_1 (or_1_out, ADD_R, SUB_R);
  or or_2 (or_2_out, ADD_I, SUB_I);
  or or_3 (or_3_out, LSL, LSR, ASR);
  or or_4 (or_4_out, MOVE, CMP);
  or or_5 (or_5_out, ADD_IMM, SUB_IMM);
  assign {Instr[15:14], Carry, ALU_Opcode, Instr[8:0]} = Instruction & bit_extender_1_out;  // AND_Gate and_1, 16 bits wide
  and and_2 (and_2_out, or_1_out, ADD_SUB);
  and and_3 (and_3_out, or_2_out, ADD_SUB);
  assign bit_extender_2_out = {{15{or_3_out}}, or_3_out};  // Bit_Extender bit_extender_2
  assign bit_extender_3_out = {{15{or_4_out}}, or_4_out};  // Bit_Extender bit_extender_3
  assign {and_4_out[15:11], RD4, and_4_out[7:0]} = bit_extender_3_out & {Instr[15:14], Carry, ALU_Opcode, Instr[8:0]};  // AND_Gate and_4, 16 bits wide
  assign bit_extender_4_out = {{15{or_5_out}}, or_5_out};  // Bit_Extender bit_extender_4
  assign {and_5_out[15:11], RDN5, and_5_out[7:0]} = bit_extender_4_out & {Instr[15:14], Carry, ALU_Opcode, Instr[8:0]};  // AND_Gate and_5, 16 bits wide
  assign bit_extender_5_out = {{15{and_2_out}}, and_2_out};  // Bit_Extender bit_extender_5
  assign bit_extender_6_out = {{15{and_3_out}}, and_3_out};  // Bit_Extender bit_extender_6
  assign {and_6_out, Imm5, RM2, RD3} = bit_extender_2_out & {Instr[15:14], Carry, ALU_Opcode, Instr[8:0]};  // AND_Gate and_6, 16 bits wide
  assign {and_7_out, RM1, RN1, RD1} = bit_extender_5_out & {Instr[15:14], Carry, ALU_Opcode, Instr[8:0]};  // AND_Gate and_7, 16 bits wide
  assign {and_8_out, imm3, RN2, RD2} = bit_extender_6_out & {Instr[15:14], Carry, ALU_Opcode, Instr[8:0]};  // AND_Gate and_8, 16 bits wide
  assign imm8 = and_4_out[7:0] | and_5_out[7:0];  // OR_Gate or_6, 8 bits wide
  assign Rm = RM1 | RM2;  // OR_Gate or_7, 3 bits wide
  assign bit_extender_7_out = {{29{imm3[2]}}, imm3};  // Bit_Extender bit_extender_7
  assign bit_extender_8_out = {{24{imm8[7]}}, imm8};  // Bit_Extender bit_extender_8
  or or_8 (or_8_out, ADD_I, SUB_I);
  assign Rn = RN1 | RN2 | RDN5;  // OR_Gate or_9, 3 bits wide
  assign Rd = RD1 | RD2 | RD3 | RD4 | RDN5;  // OR_Gate or_10, 3 bits wide
  assign Imm32 = bit_extender_7_out | bit_extender_8_out;  // OR_Gate or_11, 32 bits wide
  and and_9 (and_9_out, or_8_out, ADD_SUB);
  or or_12 (Imm32_Enable, and_9_out, MOVE, CMP, SUB_IMM, ADD_IMM);
  Multiplexer #(.select(3), .width(4)) multiplexer_1 (
    .in0(4'b1100), .in1(4'b1100), .in2(4'b1100), .in3(4'b1100), .in4(4'b1100), .in5(4'b0000), .in6(4'b0000),
    .in7(4'b0000), .out(Flags_Update_Mask), .sel({Carry, ALU_Opcode[3:2]}));

  // Other names for the same wires on the sheet: Instr[13:9] = {Carry, ALU_Opcode}

  // Notes on the sheet:
  //   Pull output low on Enable = 0
  //   Note: ALU uses Rn register for shifts. Use Rn instead of Rm for shifts (immediate) here too
  //   Note 2: MOV uses RSB ALU opcode with Imm8 reversed so that it is copied to output register
  //   Note 3: Imm32_Enable forces the use of the immediate for Rm register
endmodule
